# Fritzing sketch identifyResistance_LCD_I2C (saved by Fritzing 0.9.3b)
circuit board: 14.2139cm x 5.3979cm
breadboards: 1

parts:
  Controller = Arduino Nano (Rev3.0)
  R2(Unknown) = Resistor [tolerance=±5% resistance=4.7k package=THT]
  LCD_with_I2C = LCD1602-I2C
  Buzzer = Buzzer 12mm [package=buzzer-ccv-kit]
  R1 = Resistor [tolerance=±5% resistance=10k package=THT]

nets:
  GND: Controller.GND, LCD_with_I2C.GND, Buzzer.1, R1.Pin_0
  N1: Controller.D9, Buzzer.2
  5V: Controller.5V, R2(Unknown).Pin_1, LCD_with_I2C.VCC
  N2: Controller.A5, LCD_with_I2C.SCL
  N3: Controller.A4, LCD_with_I2C.SDA
  N4: Controller.A0, R2(Unknown).Pin_0, R1.Pin_1

notes:
  Unknown Resistor

custom parts:
  LCD1602-I2C: A standard character display, usually with 2x16 characters. Comes in many colors with LCM1602 IIC attached.

// code stored in the sketch: analog-read-test.ino
void setup()
{
	pinMode(A0, INPUT);
	Serial.begin(115200);
}

void loop()
{
  volatile unsigned int rawAdc = analogRead(A0);
  Serial.println(rawAdc);
  delay(200);
}
