# Fritzing sketch identifyResistance_LCD_Parallel (saved by Fritzing 0.9.3b)
circuit board: 14.2139cm x 5.3979cm
breadboards: 1

parts:
  Controller = Arduino Nano (Rev3.0)
  R2(Unknown) = Resistor [tolerance=±5% resistance=4.7k package=THT]
  Buzzer = Buzzer 12mm [package=buzzer-ccv-kit]
  U1 = LCD-16X2 [package=lcd-16x2]
  R2 = Trimmer Potentiometer [maximum_resistance=10kΩ package=THT]
  R1 = Resistor [tolerance=±5% resistance=10k package=THT]

nets:
  GND: Controller.GND, Buzzer.1, U1.VSS, U1.R_W, U1.K, R2.leg2, R1.Pin_0
  N1: Controller.D2, U1.DB7
  N2: Controller.D3, U1.DB6
  N3: Controller.D4, U1.DB5
  N4: Controller.D5, U1.DB4
  N5: Controller.D9, Buzzer.2
  N6: Controller.D11/MOSI, U1.E
  N7: Controller.D12/MISO, U1.RS
  5V: Controller.5V, R2(Unknown).Pin_1, U1.VDD, U1.A, R2.leg1
  N8: Controller.A0, R2(Unknown).Pin_0, R1.Pin_1
  N9: U1.VO, R2.wiper

notes:
  Unknown Resistor

// code stored in the sketch: analog-read-test.ino
void setup()
{
	pinMode(A0, INPUT);
	Serial.begin(115200);
}

void loop()
{
  volatile unsigned int rawAdc = analogRead(A0);
  Serial.println(rawAdc);
  delay(200);
}
